// Logisim project 10 bit clock.circ as structural Verilog: 1 circuit, main circuit main
module main (
  input  Clock,
  input  Clear,
  output Q0,
  output Q0_2,
  output Q0_3,
  output Q0_4,
  output Q0_5,
  output Q0_6,
  output Q0_7,
  output Q0_8,
  output Q0_9,
  output Q0_10
);

  wire d_ff_1_qn, d_ff_2_qn, d_ff_3_qn, d_ff_4_qn, d_ff_5_qn, d_ff_6_qn, d_ff_7_qn, d_ff_8_qn, d_ff_9_qn,
       d_ff_10_qn;

  D_Flip_Flop d_ff_1 (.clk(Clock), .D(d_ff_1_qn), .Q(Q0), .Qn(d_ff_1_qn), .en(1'b1), .reset(Clear));  // open: preset
  D_Flip_Flop d_ff_2 (
    .clk(d_ff_1_qn), .D(d_ff_2_qn), .Q(Q0_2), .Qn(d_ff_2_qn), .en(1'b1), .reset(Clear));  // open: preset
  D_Flip_Flop d_ff_3 (
    .clk(d_ff_2_qn), .D(d_ff_3_qn), .Q(Q0_3), .Qn(d_ff_3_qn), .en(1'b1), .reset(Clear));  // open: preset
  D_Flip_Flop d_ff_4 (
    .clk(d_ff_3_qn), .D(d_ff_4_qn), .Q(Q0_4), .Qn(d_ff_4_qn), .en(1'b1), .reset(Clear));  // open: preset
  D_Flip_Flop d_ff_5 (
    .clk(d_ff_4_qn), .D(d_ff_5_qn), .Q(Q0_5), .Qn(d_ff_5_qn), .en(1'b1), .reset(Clear));  // open: preset
  D_Flip_Flop d_ff_6 (
    .clk(d_ff_5_qn), .D(d_ff_6_qn), .Q(Q0_6), .Qn(d_ff_6_qn), .en(1'b1), .reset(Clear));  // open: preset
  D_Flip_Flop d_ff_7 (
    .clk(d_ff_6_qn), .D(d_ff_7_qn), .Q(Q0_7), .Qn(d_ff_7_qn), .en(1'b1), .reset(Clear));  // open: preset
  D_Flip_Flop d_ff_8 (
    .clk(d_ff_7_qn), .D(d_ff_8_qn), .Q(Q0_8), .Qn(d_ff_8_qn), .en(1'b1), .reset(Clear));  // open: preset
  D_Flip_Flop d_ff_9 (
    .clk(d_ff_8_qn), .D(d_ff_9_qn), .Q(Q0_9), .Qn(d_ff_9_qn), .en(1'b1), .reset(Clear));  // open: preset
  D_Flip_Flop d_ff_10 (
    .clk(d_ff_9_qn), .D(d_ff_10_qn), .Q(Q0_10), .Qn(d_ff_10_qn), .en(1'b1), .reset(Clear));  // open: preset
endmodule
