// Logisim project 4 XOR gate IC.circ as structural Verilog: 1 circuit, main circuit main
module main (
  input  Input_1,
  input  Input_2,
  input  Input_1_2,
  input  Input_2_2,
  input  Input_1_3,
  input  input_2_3,
  input  Input_1_4,
  input  input_2_4,
  output Out_1,
  output Out_1_2,
  output Out_2,
  output Out_1_3
);

  xor xor_1 (Out_1, Input_2, Input_1);
  xor xor_2 (Out_2, input_2_3, Input_1_3);
  xor xor_3 (Out_1_2, Input_2_2, Input_1_2);
  xor xor_4 (Out_1_3, input_2_4, Input_1_4);
endmodule
