// Logisim project 4 bit multiplier.circ as structural Verilog: 1 circuit, main circuit main
module main (
  input  Input_A3,
  input  Input_A2,
  input  Input_A1,
  input  Input_A0,
  input  Input_B0,
  input  Input_B1,
  input  Input_B2,
  input  Input_B3,
  input  Enable,
  output M7,
  output M6,
  output M5,
  output M4,
  output M3,
  output M2,
  output M1,
  output M0
);

  wire and_1_out, and_2_out, and_4_out, and_5_out, and_7_out, and_8_out, and_10_out, and_11_out, and_13_out,
       and_14_out, and_16_out, and_17_out, and_19_out, and_20_out, and_21_out, and_22_out, main_1_cout_3,
       main_1_sum_0, main_1_sum_1, main_1_sum_2, main_1_sum_3, main_2_cout_3, main_2_sum_0, main_2_sum_1,
       main_2_sum_2, main_2_sum_3, main_3_cout_3, main_3_sum_0, main_3_sum_1, main_3_sum_2, main_3_sum_3;

  and and_1 (and_1_out, Input_B3, Input_A2);
  and and_2 (and_2_out, Input_B3, Input_A3);
  and and_3 (M7, main_1_cout_3, Enable);
  and and_4 (and_4_out, Input_B3, Input_A1);
  and and_5 (and_5_out, Input_B3, Input_A0);
  and and_6 (M6, main_1_sum_3, Enable);
  and and_7 (and_7_out, Input_B2, Input_A2);
  and and_8 (and_8_out, Input_B2, Input_A3);
  and and_9 (M5, main_1_sum_2, Enable);
  and and_10 (and_10_out, Input_B2, Input_A0);
  and and_11 (and_11_out, Input_B2, Input_A1);
  full_adder_4_bit__main main_1 (
    .Carry_in(1'b0), .Input_B0(and_5_out), .Input_A0(main_2_sum_1), .Sum_0(main_1_sum_0),
    .Input_B1(and_4_out), .Input_A1(main_2_sum_2), .Sum_1(main_1_sum_1), .Input_B2(and_1_out),
    .Input_A2(main_2_sum_3), .Sum_2(main_1_sum_2), .Input_B3(and_2_out), .Input_A3(main_2_cout_3),
    .Sum_3(main_1_sum_3), .Enable(1'b1), .Cout_3(main_1_cout_3));  // open: Cout_0, Cout_1, Cout_2
  and and_12 (M4, main_1_sum_1, Enable);
  and and_13 (and_13_out, Input_B1, Input_A2);
  and and_14 (and_14_out, Input_B1, Input_A3);
  full_adder_4_bit__main main_2 (
    .Carry_in(1'b0), .Input_B0(and_10_out), .Input_A0(main_3_sum_1), .Sum_0(main_2_sum_0),
    .Input_B1(and_11_out), .Input_A1(main_3_sum_2), .Sum_1(main_2_sum_1), .Input_B2(and_7_out),
    .Input_A2(main_3_sum_3), .Sum_2(main_2_sum_2), .Input_B3(and_8_out), .Input_A3(main_3_cout_3),
    .Sum_3(main_2_sum_3), .Enable(1'b1), .Cout_3(main_2_cout_3));  // open: Cout_0, Cout_1, Cout_2
  and and_15 (M3, main_1_sum_0, Enable);
  and and_16 (and_16_out, Input_B1, Input_A0);
  and and_17 (and_17_out, Input_B1, Input_A1);
  full_adder_4_bit__main main_3 (
    .Carry_in(1'b0), .Input_B0(and_16_out), .Input_A0(and_22_out), .Sum_0(main_3_sum_0),
    .Input_B1(and_17_out), .Input_A1(and_19_out), .Sum_1(main_3_sum_1), .Input_B2(and_13_out),
    .Input_A2(and_20_out), .Sum_2(main_3_sum_2), .Input_B3(and_14_out), .Input_A3(1'b0),
    .Sum_3(main_3_sum_3), .Enable(1'b1), .Cout_3(main_3_cout_3));  // open: Cout_0, Cout_1, Cout_2
  and and_18 (M2, main_2_sum_0, Enable);
  and and_19 (and_19_out, Input_B0, Input_A2);
  and and_20 (and_20_out, Input_B0, Input_A3);
  and and_21 (and_21_out, Input_B0, Input_A0);
  and and_22 (and_22_out, Input_B0, Input_A1);
  and and_23 (M1, main_3_sum_0, Enable);
  and and_24 (M0, and_21_out, Enable);
endmodule
