// Logisim project ALU circuit mains.circ as structural Verilog: 1 circuit, main circuit main
module main (
  input  [3:0] Input_A,
  input  [3:0] Input_B,
  input  Op_code_decoder,
  input  in_4,
  input  in_5,
  input  in_6,
  input  in_7,
  output [7:0] out_8
);

  wire and_1_out, and_2_out, and_3_out, and_4_out, and_9_out, clock_1_out, comparator_1_eq, comparator_1_gt,
       comparator_1_lt, decoder_1_out0, decoder_1_out1, decoder_1_out2, decoder_1_out3, decoder_1_out6,
       decoder_1_out7, main_3_cout_2, not_1_out, not_3_out, Odd_Parity_out, or_1_out, or_2_out, xor_1_out,
       xor_2_out, xor_3_out, xor_4_out, xor_5_out, xor_6_out, xor_7_out, xor_8_out, xor_9_out;
  wire [3:0] and_8_out, main_1_sum_0, main_4_out_2, main_4_out_2_2, main_4_out_2_3, not_2_out;
  wire [4:0] main_3_sum_0;
  wire [7:0] bit_extender_1_out, bit_extender_2_out, bit_extender_3_out, main_2_m0, main_5_q0;

  xor xor_1 (xor_1_out, main_3_sum_0[3], main_3_sum_0[2]);
  xor xor_2 (xor_2_out, main_3_sum_0[3], main_3_sum_0[3]);
  xor xor_3 (xor_3_out, main_3_sum_0[3], main_3_sum_0[1]);
  xor xor_4 (xor_4_out, main_3_sum_0[3], main_3_sum_0[0]);
  full_adder_4_bit__main main_1 (
    .Carry_in(xor_2_out), .Input_B0(main_3_sum_0[3]), .Input_A0(xor_4_out), .Sum_0(main_1_sum_0[0]),
    .Input_B1(in_6), .Input_A1(xor_3_out), .Sum_1(main_1_sum_0[1]), .Input_B2(in_6), .Input_A2(xor_1_out),
    .Sum_2(main_1_sum_0[2]), .Input_B3(in_6), .Input_A3(xor_2_out), .Sum_3(main_1_sum_0[3]), .Enable(in_7));  // open: Cout_0, Cout_1, Cout_2, Cout_3
  Hex_Digit_Display hex_digit_display_1 (.value(Input_A));  // open: dp
  _4_bit_multiplier_main main_2 (
    .Input_B0(Input_B[0]), .Input_B1(Input_B[1]), .Input_B2(Input_B[2]), .Input_B3(Input_B[3]),
    .Input_A3(Input_A[3]), .Input_A2(Input_A[2]), .Input_A1(Input_A[1]), .Input_A0(Input_A[0]),
    .Enable(decoder_1_out6), .M7(main_2_m0[7]), .M6(main_2_m0[6]), .M5(main_2_m0[5]), .M4(main_2_m0[4]),
    .M3(main_2_m0[3]), .M2(main_2_m0[2]), .M1(main_2_m0[1]), .M0(main_2_m0[0]));
  full_adder_4_bit__main main_3 (
    .Carry_in(or_1_out), .Input_B0(Input_A[0]), .Input_A0(and_4_out), .Sum_0(main_3_sum_0[0]),
    .Input_B1(Input_A[1]), .Input_A1(and_3_out), .Sum_1(main_3_sum_0[1]), .Input_B2(Input_A[2]),
    .Input_A2(and_2_out), .Cout_2(main_3_cout_2), .Sum_2(main_3_sum_0[2]), .Input_B3(Input_A[3]),
    .Input_A3(and_1_out), .Sum_3(main_3_sum_0[3]), .Enable(or_2_out), .Cout_3(main_3_sum_0[4]));  // open: Cout_0, Cout_1
  assign bit_extender_1_out = {{4{1'b0}}, main_1_sum_0};  // Bit_Extender bit_extender_1
  and and_1 (and_1_out, xor_5_out, not_1_out);
  xor xor_5 (xor_5_out, Input_B[3], decoder_1_out1);
  and and_2 (and_2_out, xor_6_out, not_1_out);
  assign bit_extender_2_out = {{3{1'b0}}, main_3_sum_0};  // Bit_Extender bit_extender_2
  Multiplexer #(.select(3), .width(8)) multiplexer_1 (
    .in0(bit_extender_2_out), .in1(bit_extender_1_out), .in2(bit_extender_3_out), .in3(bit_extender_2_out),
    .in6(main_2_m0), .in7(main_5_q0), .out(out_8), .sel({Op_code_decoder, in_4, in_5}));  // open: in4, in5, en
  Hex_Digit_Display hex_digit_display_2 (.value(Input_B));  // open: dp
  xor xor_6 (xor_6_out, Input_B[2], decoder_1_out1);
  xor xor_7 (xor_7_out, Input_B[1], decoder_1_out1);
  and and_3 (and_3_out, xor_7_out, not_1_out);
  and and_4 (and_4_out, xor_8_out, not_1_out);
  or or_1 (or_1_out, decoder_1_out1, decoder_1_out3);
  xor xor_8 (xor_8_out, Input_B[0], decoder_1_out1);
  or or_2 (or_2_out, decoder_1_out0, decoder_1_out1, decoder_1_out3);
  not not_1 (not_1_out, decoder_1_out3);
  LED NEGETIVE (.in(main_3_sum_0[3]));
  xor xor_9 (xor_9_out, main_3_sum_0[4], main_3_cout_2);
  LED OVERFLOW (.in(xor_9_out));
  and and_5 (and_8_out[3], Input_A[3], decoder_1_out2);
  binary_to_bcd_rom_main main_4 (.out_2({main_4_out_2_3, main_4_out_2_2, main_4_out_2}), .in_1(out_8));
  Hex_Digit_Display hex_digit_display_3 (.value(main_4_out_2_3));  // open: dp
  and and_6 (and_8_out[1], Input_A[1], decoder_1_out2);
  and and_7 (and_8_out[2], Input_A[2], decoder_1_out2);
  Hex_Digit_Display hex_digit_display_4 (.value(main_4_out_2_2));  // open: dp
  and and_8 (and_8_out[0], Input_A[0], decoder_1_out2);
  assign not_2_out = ~and_8_out;  // NOT_Gate not_2, 4 bits wide
  _10_bit_clock_main main_5 (
    .Clock(and_9_out), .Q0(main_5_q0[0]), .Q0_2(main_5_q0[1]), .Q0_3(main_5_q0[2]), .Q0_4(main_5_q0[3]),
    .Q0_5(main_5_q0[4]), .Q0_6(main_5_q0[5]), .Q0_7(main_5_q0[6]), .Q0_8(main_5_q0[7]), .Clear(not_3_out));  // open: Q0_9, Q0_10
  Hex_Digit_Display hex_digit_display_5 (.value(main_4_out_2));  // open: dp
  assign bit_extender_3_out = {{4{1'b0}}, not_2_out};  // Bit_Extender bit_extender_3
  not not_3 (not_3_out, decoder_1_out7);
  LED led_1 (.in(comparator_1_gt));
  LED led_2 (.in(comparator_1_eq));
  Comparator #(.width(4), .mode("unsigned")) comparator_1 (
    .a(Input_A), .b(Input_B), .gt(comparator_1_gt), .eq(comparator_1_eq), .lt(comparator_1_lt));
  LED led_3 (.in(comparator_1_lt));
  and and_9 (and_9_out, decoder_1_out7, clock_1_out);
  xor Odd_Parity (Odd_Parity_out, Input_A[3], Input_A[2], Input_A[1], Input_A[0]);
  LED led_4 (.in(Odd_Parity_out));
  Clock clock_1 (.out(clock_1_out));
  Decoder #(.select(3)) decoder_1 (
    .out0(decoder_1_out0), .out1(decoder_1_out1), .out2(decoder_1_out2), .out3(decoder_1_out3),
    .out6(decoder_1_out6), .out7(decoder_1_out7), .sel({Op_code_decoder, in_4, in_5}));  // open: out4, out5, en

  // Notes on the sheet:
  //   0 - ADD 
  //   1 - SUB
  //   2 - INV
  //   3 - INC
  //   4 - comp
  //   5 - parity
  //   6 - multiply
  //   7 - counter
endmodule
