// Logisim project Binary to BCD converter.circ as structural Verilog: 1 circuit, main circuit main
module main (
  input  A,
  input  B,
  input  C,
  input  D,
  output B1,
  output B2,
  output B4,
  output B3,
  output B5
);

  wire and_1_out, and_2_out, and_4_out, and_5_out, and_6_out, and_7_out;

  and and_1 (and_1_out, A, B);
  and and_2 (and_2_out, B, C);
  or or_1 (B5, and_1_out, and_2_out);
  and and_3 (B4, A, ~B, ~C);  // AND_Gate
  and and_4 (and_4_out, ~A, B);  // AND_Gate
  or or_2 (B3, and_4_out, and_5_out);
  and and_5 (and_5_out, C, B);
  and and_6 (and_6_out, ~A, C);  // AND_Gate
  or or_3 (B2, and_6_out, and_7_out);
  and and_7 (and_7_out, A, B, ~C);  // AND_Gate

  assign B1 = D;
endmodule
