// Logisim project full adder 4 bit .circ as structural Verilog: 1 circuit, main circuit main
module main (
  input  Input_B0,
  input  Carry_in,
  input  Input_A0,
  input  Input_B1,
  input  Input_A1,
  input  Input_B2,
  input  Input_A2,
  input  Enable,
  input  Input_B3,
  input  Input_A3,
  output Cout_0,
  output Cout_1,
  output Sum_0,
  output Sum_1,
  output Cout_2,
  output Sum_2,
  output Sum_3,
  output Cout_3
);

  wire and_1_out, and_2_out, and_4_out, and_5_out, and_7_out, and_9_out, and_11_out, and_12_out, or_1_out,
       xor_1_out, xor_2_out, xor_3_out, xor_4_out, xor_5_out, xor_6_out, xor_7_out, xor_8_out;

  and and_1 (and_1_out, Input_A3, Input_B3);
  or or_1 (or_1_out, and_1_out, and_2_out);
  and and_2 (and_2_out, xor_1_out, Cout_2);
  xor xor_1 (xor_1_out, Input_B3, Input_A3);
  xor xor_2 (xor_2_out, Cout_2, xor_1_out);
  and and_3 (Cout_3, or_1_out, Enable);
  and and_4 (and_4_out, Input_A2, Input_B2);
  or or_2 (Cout_2, and_4_out, and_5_out);
  and and_5 (and_5_out, xor_3_out, Cout_1);
  and and_6 (Sum_3, xor_2_out, Enable);
  xor xor_3 (xor_3_out, Input_B2, Input_A2);
  xor xor_4 (xor_4_out, Cout_1, xor_3_out);
  and and_7 (and_7_out, Input_A1, Input_B1);
  or or_3 (Cout_1, and_7_out, and_9_out);
  and and_8 (Sum_2, xor_4_out, Enable);
  and and_9 (and_9_out, xor_5_out, Cout_0);
  xor xor_5 (xor_5_out, Input_B1, Input_A1);
  xor xor_6 (xor_6_out, Cout_0, xor_5_out);
  and and_10 (Sum_1, xor_6_out, Enable);
  and and_11 (and_11_out, Input_A0, Input_B0);
  and and_12 (and_12_out, xor_7_out, Carry_in);
  or or_4 (Cout_0, and_11_out, and_12_out);
  and and_13 (Sum_0, xor_8_out, Enable);
  xor xor_7 (xor_7_out, Input_B0, Input_A0);
  xor xor_8 (xor_8_out, Carry_in, xor_7_out);
endmodule
