// Logisim project full adder.circ as structural Verilog: 1 circuit, main circuit main
module main (
  input  imput_2,
  input  Carry,
  input  imput_1,
  output Sum,
  output Carry_out
);

  wire and_1_out, and_2_out, xor_1_out;

  and and_1 (and_1_out, imput_1, imput_2);
  and and_2 (and_2_out, xor_1_out, Carry);
  or or_1 (Carry_out, and_1_out, and_2_out);
  xor xor_1 (xor_1_out, imput_2, imput_1);
  xor xor_2 (Sum, Carry, xor_1_out);
endmodule
